// Digital circuit lc3.dig as structural Verilog
module lc3 (
  input  Clk,
  input  [15:0] Breakpoint,
  input  Enabled
);

  wire ACV, ADDR1MUX, BEN, comparator_1_eq, GateALU, GateMARMUX, GateMDR, GatePC, GatePC_1, GatePSR, GateSP,
       GateVector, lc3_cc_logic_1_n, lc3_cc_logic_1_p, lc3_cc_logic_1_z, LD_ACV, LD_BEN, LD_CC, LD_DDR,
       LD_IR, LD_MAR, LD_MDR, LD_PC, LD_Priv, LD_REG, LD_SavedSSP, LD_SavedUSP, LD_Vector, MARMUX, MIO_EN, N,
       P, PSR_15, PSRMux, R, R_W, Set_Priv, SR2MUX, TableMux, Z;
  wire [1:0] ADDR2MUX, ALUK, DRMUX, PCMUX, SPMUX, SR1MUX;
  wire [2:0] IR_2_0, multiplexer_6_out, multiplexer_8_out, SR1;
  wire [4:0] Immed;
  wire [4:1] IR_15_11;
  wire [5:0] State;
  wire [15:0] _1_s, ADDER, Bus, DSR, KBDR, KBSR, keyboard_1_d, lc3_alu_2_alu, lc3_register_file_1_sr2_out,
       MAR, MDR_out, Memory_d_out, multiplexer_1_out, multiplexer_2_out, multiplexer_3_out,
       multiplexer_4_out, multiplexer_5_out, multiplexer_7_out, PC, plus_1_s, SEXT_2_out, SEXT_3_out,
       SEXT_4_out, SEXT_out, SR1_OUT;
  wire [15:15] KB_Data;

  lc3_breakpoint lc3_breakpoint_1 (.Breakpoint(Breakpoint), .PC(PC), .State(State), .en(Enabled));
  // lc3_halt lc3_halt_1: pin names not known; wires that end beside it: MAR, MDR_out, R_W, Bus
  Register #(.Bits(16)) IR (.D(Bus), .C(Clk), .en(LD_IR), .Q({IR_15_11, IR_2_0, SR1, SR2MUX, Immed}));
  BitExtender #(.inputBits(6)) SEXT (.in({SR2MUX, Immed}), .out(SEXT_out));
  BitExtender #(.inputBits(9)) SEXT_2 (.in({SR1, SR2MUX, Immed}), .out(SEXT_2_out));
  BitExtender #(.inputBits(11)) SEXT_3 (.in({IR_2_0[1:0], SR1, SR2MUX, Immed}), .out(SEXT_3_out));
  assign Bus = GateMARMUX ? multiplexer_1_out : 16'bz;  // Driver driver_1
  Multiplexer #(.Bits(16)) multiplexer_1 (
    .sel(MARMUX), .in_0({{8{1'b0}}, SR1[1:0], SR2MUX, Immed}), .in_1(ADDER), .out(multiplexer_1_out));
  Multiplexer #(.Selector_Bits(2), .Bits(16)) multiplexer_2 (
    .sel(ADDR2MUX), .in_0({16{1'b0}}), .in_1(SEXT_out), .in_2(SEXT_2_out), .in_3(SEXT_3_out),
    .out(multiplexer_2_out));
  Register u_N (.D(lc3_cc_logic_1_n), .C(Clk), .en(LD_CC), .Q(N));
  Multiplexer #(.Bits(16)) multiplexer_3 (.sel(ADDR1MUX), .in_0(PC), .in_1(SR1_OUT), .out(multiplexer_3_out));
  Register u_Z (.D(lc3_cc_logic_1_z), .C(Clk), .en(LD_CC), .Q(Z));
  lc3_cc_logic lc3_cc_logic_1 (.D_in(Bus), .N(lc3_cc_logic_1_n), .Z(lc3_cc_logic_1_z), .P(lc3_cc_logic_1_p));
  lc3_alu lc3_alu_1 (.ALU(ADDER), .A(multiplexer_2_out), .B(multiplexer_3_out), .ALUK(2'b00));
  Register u_P (.D(lc3_cc_logic_1_p), .C(Clk), .en(LD_CC), .Q(P));
  assign Bus = GateMDR ? MDR_out : 16'bz;  // Driver driver_2
  Register #(.Bits(16)) MDR (.D(multiplexer_4_out), .C(Clk), .en(LD_MDR), .Q(MDR_out));
  lc3_control lc3_control_1 (
    .Clk(Clk), .INT(1'b0), .R(R), .IR_15_11({IR_15_11, IR_2_0[2]}), .BEN(BEN), .PSR_15(PSR_15), .ACV(ACV),
    .LD_MAR(LD_MAR), .LD_MDR(LD_MDR), .LD_IR(LD_IR), .LD_BEN(LD_BEN), .LD_REG(LD_REG), .LD_CC(LD_CC),
    .LD_PC(LD_PC), .LD_Priv(LD_Priv), .LD_SavedSSP(LD_SavedSSP), .LD_SavedUSP(LD_SavedUSP),
    .LD_Vector(LD_Vector), .LD_ACV(LD_ACV), .GatePC(GatePC), .GateMDR(GateMDR), .GateALU(GateALU),
    .GateMARMUX(GateMARMUX), .GateVector(GateVector), .GatePC_1(GatePC_1), .GatePSR(GatePSR),
    .GateSP(GateSP), .PCMUX(PCMUX), .DRMUX(DRMUX), .SR1MUX(SR1MUX), .ADDR2MUX(ADDR2MUX), .SPMUX(SPMUX),
    .ALUK(ALUK), .ADDR1MUX(ADDR1MUX), .MARMUX(MARMUX), .TableMUX(TableMux), .PSRMUX(PSRMux), .MIO_EN(MIO_EN),
    .R_W(R_W), .Set_Priv(Set_Priv), .State(State));  // open: LD_Priority, VectorMUX
  Multiplexer #(.Bits(16)) multiplexer_4 (.sel(MIO_EN), .in_0(Bus), .in_1(Memory_d_out), .out(multiplexer_4_out));
  assign Bus = GatePC_1 ? _1_s : 16'bz;  // Driver driver_3
  Add #(.Bits(16)) _1 (.a(PC), .b({16{1'b1}}), .c_i(1'b0), .s(_1_s));  // open: c_o
  lc3_memory Memory (
    .Addr(MAR), .D_in(MDR_out), .R_W(R_W), .Clk(Clk), .MIO_EN(MIO_EN), .KBSR(KBSR), .KBDR(KBDR), .DSR(DSR),
    .D_out(Memory_d_out), .R(R), .LD_DDR(LD_DDR));  // open: LD_KBSR, LD_DSR
  Add #(.Bits(16)) plus_1 (.a(PC), .b(16'h1), .c_i(1'b0), .s(plus_1_s));  // open: c_o
  Multiplexer #(.Selector_Bits(2), .Bits(16)) multiplexer_5 (
    .sel(PCMUX), .in_0(plus_1_s), .in_1(Bus), .in_2(ADDER), .in_3({16{1'b0}}), .out(multiplexer_5_out));
  Register #(.Bits(16)) u_MAR (.D(Bus), .C(Clk), .en(LD_MAR), .Q(MAR));
  Comparator #(.Bits(16)) comparator_1 (.a(16'hfe02), .b(MAR), .eq(comparator_1_eq));  // open: gt, lt
  pc #(.applicationType("IVERILOG"), .CodeFile("\\home\\allan\\cs061\\LC3_realized\\lc3-pc.v")) u_pc (
    .D(multiplexer_5_out), .C(Clk), .en(LD_PC), .Q(PC));
  Keyboard keyboard_1 (.C(Clk), .en(comparator_1_eq), .D(keyboard_1_d), .av(KB_Data[15]));
  assign Bus = GatePC ? PC : 16'bz;  // Driver driver_4
  Multiplexer #(.Selector_Bits(2), .Bits(3)) multiplexer_6 (
    .sel(DRMUX), .in_0(IR_2_0), .in_1(3'b111), .in_2(3'b110), .in_3(3'b000), .out(multiplexer_6_out));
  Register #(.Bits(16)) u_KBSR (.D({KB_Data[15], {15{1'b0}}}), .C(Clk), .en(KB_Data[15]), .Q(KBSR));
  Register #(.Bits(16)) u_KBDR (.D(keyboard_1_d), .C(Clk), .en(KB_Data[15]), .Q(KBDR));
  BitExtender #(.inputBits(5)) SEXT_4 (.in(Immed), .out(SEXT_4_out));
  // Probe State on State
  lc3_register_file lc3_register_file_1 (
    .Clk(Clk), .Data(Bus), .LD_Reg(LD_REG), .DR(multiplexer_6_out), .SR1(multiplexer_8_out),
    .SR2(Immed[2:0]), .SR2_OUT(lc3_register_file_1_sr2_out), .SR1_OUT(SR1_OUT));
  Multiplexer #(.Bits(16)) multiplexer_7 (
    .sel(SR2MUX), .in_0(lc3_register_file_1_sr2_out), .in_1(SEXT_4_out), .out(multiplexer_7_out));
  lc3_alu lc3_alu_2 (.ALU(lc3_alu_2_alu), .A(SR1_OUT), .B(multiplexer_7_out), .ALUK(ALUK));
  assign Bus = GateALU ? lc3_alu_2_alu : 16'bz;  // Driver driver_5
  Multiplexer #(.Selector_Bits(2), .Bits(3)) multiplexer_8 (
    .sel(SR1MUX), .in_0(IR_2_0), .in_1(SR1), .in_2(3'b110), .in_3(3'b000), .out(multiplexer_8_out));
  Register #(.Bits(16)) u_DSR (.D(16'h8000), .C(Clk), .en(Clk), .Q(DSR));
  Terminal terminal_1 (.D(MDR_out[7:0]), .C(Clk), .en(LD_DDR));
  lc3_details lc3_details_1 (
    .Clk(Clk), .LD_SavedSSP(LD_SavedSSP), .LD_SavedUSP(LD_SavedUSP), .GateSP(GateSP), .SPMUX(SPMUX),
    .SR1_Val(SR1_OUT), .TableMux(TableMux), .LD_Vector(LD_Vector), .GateVector(GateVector), .N(N), .Z(Z),
    .P(P), .IR_2_0(IR_2_0), .LD_BEN(LD_BEN), .LD_ACV(LD_ACV), .Set_Priv(Set_Priv), .PSRMux(PSRMux),
    .GatePSR(GatePSR), .LD_Priv(LD_Priv), .Bus(Bus), .GatedSP(Bus), .GatedVector(Bus), .GatedPSR(Bus),
    .BEN(BEN), .ACV(ACV), .PSR_15(PSR_15));

  // Other names for the same wires on the sheet: SR2[2:0] = Immed[2:0]; IR_15_11[0] = IR_2_0[2]

  // Notes on the sheet:
  //   Breakpoint: default 65535
  //   Enabled: default 1
  //   Debug/Controls
  //   Input
  //   Output
endmodule
